// Logisim project main2_works.circ as structural Verilog: 13 circuits, main circuit main
module main (
  output BEGIN,
  output [3:0] out_2,
  output [7:0] out_3,
  output [7:0] out_4,
  output [7:0] out_5,
  output [7:0] out_6,
  output [7:0] out_7,
  output [7:0] out_8,
  output [7:0] out_9,
  output [7:0] out_10,
  output [7:0] out_11,
  output [3:0] correct,
  output [3:0] mistake,
  output LOST,
  output WON,
  output [7:0] out_16,
  output [3:0] mistake_2,
  output [7:0] out_18,
  output [7:0] out_19,
  output [7:0] out_20,
  output [7:0] out_21,
  output [7:0] out_22,
  output MISTAKE_3,
  output [7:0] out_24,
  output CORRECT_2,
  output [7:0] out_26,
  output [7:0] guess
);

  wire A_out, B_out, C_out, clearWord_out, clock_1_out, comparator_2_eq, COMPUTER_SCORE_a_2,
       COMPUTER_SCORE_b_2, COMPUTER_SCORE_c_2, COMPUTER_SCORE_d_2, COMPUTER_SCORE_e, COMPUTER_SCORE_f,
       COMPUTER_SCORE_g, control_unit_check_word_1_checked, control_unit_check_word_1_clear_count,
       control_unit_check_word_1_count_n, control_unit_check_word_1_swt, control_unit_get_word_1_l1,
       control_unit_get_word_1_l2, control_unit_get_word_1_l3, control_unit_get_word_1_l4,
       control_unit_get_word_1_l5, control_unit_get_word_1_l6, control_unit_get_word_1_l7,
       control_unit_get_word_1_l8, control_unit_get_word_1_l_n, D_out, datapath_check_word_1_eq_count,
       datapath_check_word_1_eq_l_t_g, display_1_clear_screen, display_7_segment_1_a_2,
       display_7_segment_1_b_2, display_7_segment_1_c_2, display_7_segment_1_d_2, display_7_segment_1_e,
       display_7_segment_1_f, display_7_segment_1_g, E_out, enter_out, F_out, G_out, GAME_END_out, H_out,
       I_out, J_out, K_out, L_out, M_out, main_loop_control_unit_1_clear_mistake,
       main_loop_control_unit_1_l_guess, main_loop_control_unit_1_s_l, main_loop_control_unit_1_s_l_0,
       main_loop_control_unit_1_start_check_fun, main_loop_datapath_1_won, N_out, not_1_out, not_2_out,
       O_out, or_1_out, P_out, Q_out, R_out, Replay_out, restart_out, S_out, start_prime_out, T_out, U_out,
       USER_SCORE_a_2, USER_SCORE_b_2, USER_SCORE_c_2, USER_SCORE_d_2, USER_SCORE_e, USER_SCORE_f,
       USER_SCORE_g, V_out, W_out, won_count_out, X_out, Y_out, Z_out;
  wire [3:0] datapath_check_word_1_counter, loses_q, wins_q;
  wire [7:0] datapath_check_word_1_current_letter, display_1_display_in, led_matrix_1_col_1,
       led_matrix_1_col_2, led_matrix_1_col_3, led_matrix_1_col_4, led_matrix_1_col_5, multiplexer_1_out,
       multiplexer_2_out, multiplexer_3_out, multiplexer_4_out, multiplexer_5_out, multiplexer_6_out,
       multiplexer_7_out, multiplexer_8_out;

  Button A (.out(A_out));
  Button B (.out(B_out));
  Button C (.out(C_out));
  Button D (.out(D_out));
  Button E (.out(E_out));
  Button F (.out(F_out));
  Button G (.out(G_out));
  Button H (.out(H_out));
  Button I (.out(I_out));
  Button J (.out(J_out));
  Button K (.out(K_out));
  Button L (.out(L_out));
  Button M (.out(M_out));
  Button N (.out(N_out));
  Button O (.out(O_out));
  Button P (.out(P_out));
  Button Q (.out(Q_out));
  Button R (.out(R_out));
  Button S (.out(S_out));
  Button T (.out(T_out));
  Button U (.out(U_out));
  Button V (.out(V_out));
  Button W (.out(W_out));
  Button X (.out(X_out));
  Button Y (.out(Y_out));
  Button Z (.out(Z_out));
  keyboard keyboard_1 (
    .A(A_out), .B(B_out), .C(C_out), .D(D_out), .E(E_out), .F(F_out), .G(G_out), .H(H_out), .I(I_out),
    .J(J_out), .K(K_out), .L(L_out), .M(M_out), .N(N_out), .O(O_out), .P(P_out), .Q(Q_out), .R(R_out),
    .S(S_out), .T(T_out), .U(U_out), .V(V_out), .W(W_out), .X(X_out), .Y(Y_out), .Z(Z_out), .key_output(out_5));
  Button enter (.out(enter_out));
  datapath_check_word datapath_check_word_1 (
    .letter_n(out_2), .count_n(control_unit_check_word_1_count_n), .T1(out_16), .L1(out_3), .T2(out_18),
    .L2(out_4), .T3(out_19), .L3(out_6), .T4(out_20), .guess(guess), .L4(out_7), .T5(out_21), .L5(out_8),
    .t6(out_22), .L6(out_9), .T7(out_24), .L7(out_10), .T8(out_26), .L8(out_11),
    .s_w_t(control_unit_check_word_1_swt), .counter(datapath_check_word_1_counter),
    .eq_count(datapath_check_word_1_eq_count), .clear_count(control_unit_check_word_1_clear_count),
    .EQ_L_T_G(datapath_check_word_1_eq_l_t_g), .current_letter(datapath_check_word_1_current_letter));
  control_unit_get_word control_unit_get_word_1 (
    .START(start_prime_out), .ENTER(enter_out), .L1(control_unit_get_word_1_l1),
    .L2(control_unit_get_word_1_l2), .L3(control_unit_get_word_1_l3), .L4(control_unit_get_word_1_l4),
    .L5(control_unit_get_word_1_l5), .L6(control_unit_get_word_1_l6), .L7(control_unit_get_word_1_l7),
    .L8(control_unit_get_word_1_l8), .L_N(control_unit_get_word_1_l_n), .\begin (BEGIN),
    .replay(clearWord_out));
  Button start_prime (.out(start_prime_out));
  Button restart (.out(restart_out));
  Clock clock_1 (.out(clock_1_out));
  control_unit_check_word control_unit_check_word_1 (
    .eq_l_t_g(datapath_check_word_1_eq_l_t_g), .eq_count(datapath_check_word_1_eq_count),
    .begin_check(main_loop_control_unit_1_start_check_fun), .count_n(control_unit_check_word_1_count_n),
    .mistake(MISTAKE_3), .swt(control_unit_check_word_1_swt), .correct(CORRECT_2),
    .clear_count(control_unit_check_word_1_clear_count), .checked(control_unit_check_word_1_checked));  // open: L_T_new
  datapath_get_word datapath_get_word_1 (
    .L_N(control_unit_get_word_1_l_n), .L_1(control_unit_get_word_1_l1), .L_2(control_unit_get_word_1_l2),
    .L_3(control_unit_get_word_1_l3), .lkey_input(out_5), .L_4(control_unit_get_word_1_l4),
    .L_5(control_unit_get_word_1_l5), .L_6(control_unit_get_word_1_l6), .L_7(control_unit_get_word_1_l7),
    .L_8(control_unit_get_word_1_l8), .CLK(clock_1_out), .ClearWord(clearWord_out), .n_letters(out_2),
    .letter_1(out_3), .letter_2(out_4), .letter_3(out_6), .letter_4(out_7), .letter_5(out_8),
    .letttere_6(out_9), .letter_7(out_10), .letter_8(out_11));
  and Replay (Replay_out, restart_out, GAME_END_out);
  or or_1 (or_1_out, LOST, main_loop_datapath_1_won);
  Multiplexer #(.width(8)) multiplexer_1 (
    .in0(out_3), .in1(out_16), .out(multiplexer_1_out), .sel(not_1_out));  // open: en
  Multiplexer #(.width(8)) multiplexer_2 (
    .in0(out_4), .in1(out_18), .out(multiplexer_2_out), .sel(not_1_out));  // open: en
  Multiplexer #(.width(8)) multiplexer_3 (
    .in0(out_6), .in1(out_19), .out(multiplexer_3_out), .sel(not_1_out));  // open: en
  Multiplexer #(.width(8)) multiplexer_4 (
    .in0(out_7), .in1(out_20), .out(multiplexer_4_out), .sel(not_1_out));  // open: en
  Multiplexer #(.width(8)) multiplexer_5 (
    .in0(out_8), .in1(out_21), .out(multiplexer_5_out), .sel(not_1_out));  // open: en
  Multiplexer #(.width(8)) multiplexer_6 (
    .in0(out_9), .in1(out_22), .out(multiplexer_6_out), .sel(not_1_out));  // open: en
  Multiplexer #(.width(8)) multiplexer_7 (
    .in0(out_10), .in1(out_24), .out(multiplexer_7_out), .sel(not_1_out));  // open: en
  Multiplexer #(.width(8)) multiplexer_8 (
    .in0(out_11), .in1(out_26), .out(multiplexer_8_out), .sel(not_1_out));  // open: en
  or GAME_END (GAME_END_out, WON, LOST);
  main_loop_control_unit main_loop_control_unit_1 (
    .\begin (BEGIN), .e(enter_out), .res(Replay_out), .checked(control_unit_check_word_1_checked),
    .won(main_loop_datapath_1_won), .lsot(LOST), .S_L_0(main_loop_control_unit_1_s_l_0),
    .S_L(main_loop_control_unit_1_s_l), .clear_mistake(main_loop_control_unit_1_clear_mistake),
    .L_guess(main_loop_control_unit_1_l_guess), .start_check_fun(main_loop_control_unit_1_start_check_fun));  // open: clear_reset
  not not_1 (not_1_out, or_1_out);
  and clearWord (clearWord_out, Replay_out, BEGIN);
  display_7_segment display_7_segment_1 (
    .D(out_2[3]), .C(out_2[2]), .B(out_2[1]), .A(out_2[0]), .a_2(display_7_segment_1_a_2),
    .b_2(display_7_segment_1_b_2), .c_2(display_7_segment_1_c_2), .d_2(display_7_segment_1_d_2),
    .e(display_7_segment_1_e), .f(display_7_segment_1_f), .g(display_7_segment_1_g));
  _7_Segment_Display u_7_segment_display_1 (
    .g(display_7_segment_1_g), .f(display_7_segment_1_f), .a(display_7_segment_1_a_2),
    .b(display_7_segment_1_b_2), .e(display_7_segment_1_e), .d(display_7_segment_1_d_2),
    .c(display_7_segment_1_c_2));  // open: dp
  main_loop_datapath main_loop_datapath_1 (
    .mistake_incrt(MISTAKE_3), .cllear_mistake(main_loop_control_unit_1_clear_mistake), .n_letter(out_2),
    .S_COUNT(datapath_check_word_1_counter), .S_L_1(CORRECT_2), .S_L_0(main_loop_control_unit_1_s_l_0),
    .guess_key_in(out_5), .L_GUESS(main_loop_control_unit_1_l_guess),
    .new_t_from_check(datapath_check_word_1_current_letter), .S_L(main_loop_control_unit_1_s_l),
    .clear_reset(Replay_out), .CLK(clock_1_out), .L_T_update(CORRECT_2), .enable_mistake(MISTAKE_3),
    .enable_correct(CORRECT_2), .lost(LOST), .mistake_out(mistake), .correct_out(correct),
    .won(main_loop_datapath_1_won), .T_1(out_16), .mistake_count(mistake_2), .T_2(out_18), .T_3(out_19),
    .T_4(out_20), .T_5(out_21), .T_6(out_22), .T_7(out_24), .T_8(out_26), .guess_out(guess));
  Counter #(.width(4), .max('hf)) wins (.count(1'b1), .Q(wins_q), .clk(won_count_out));  // open: load, D, carry, clr
  Comparator #(.width(4), .mode("unsigned")) comparator_1 (.a(correct), .b(out_2), .eq(WON));  // open: gt, lt
  display_7_segment USER_SCORE (
    .D(wins_q[3]), .C(wins_q[2]), .B(wins_q[1]), .A(wins_q[0]), .a_2(USER_SCORE_a_2), .b_2(USER_SCORE_b_2),
    .c_2(USER_SCORE_c_2), .d_2(USER_SCORE_d_2), .e(USER_SCORE_e), .f(USER_SCORE_f), .g(USER_SCORE_g));
  _7_Segment_Display u_7_segment_display_2 (
    .g(USER_SCORE_g), .f(USER_SCORE_f), .a(USER_SCORE_a_2), .b(USER_SCORE_b_2), .e(USER_SCORE_e),
    .d(USER_SCORE_d_2), .c(USER_SCORE_c_2));  // open: dp
  Counter #(.width(4), .max('hf)) loses (.count(1'b1), .Q(loses_q), .clk(LOST));  // open: load, D, carry, clr
  not not_2 (not_2_out, comparator_2_eq);
  and won_count (won_count_out, not_2_out, BEGIN, WON);
  display_7_segment COMPUTER_SCORE (
    .D(loses_q[3]), .C(loses_q[2]), .B(loses_q[1]), .A(loses_q[0]), .a_2(COMPUTER_SCORE_a_2),
    .b_2(COMPUTER_SCORE_b_2), .c_2(COMPUTER_SCORE_c_2), .d_2(COMPUTER_SCORE_d_2), .e(COMPUTER_SCORE_e),
    .f(COMPUTER_SCORE_f), .g(COMPUTER_SCORE_g));
  Comparator #(.width(4), .mode("unsigned")) comparator_2 (
    .a(correct), .b(4'b0000), .eq(comparator_2_eq));  // open: gt, lt
  DotMatrix #(.matrixrows(8)) dotmatrix_1 (
    .col0(led_matrix_1_col_1), .col1(led_matrix_1_col_2), .col2(led_matrix_1_col_3),
    .col3(led_matrix_1_col_4), .col4(led_matrix_1_col_5));
  led_matrix led_matrix_1 (
    .select_mistake(mistake), .col_1(led_matrix_1_col_1), .col_2(led_matrix_1_col_2),
    .col_3(led_matrix_1_col_3), .col_4(led_matrix_1_col_4), .col_5(led_matrix_1_col_5));
  display display_1 (
    ._1(multiplexer_1_out), ._2(multiplexer_2_out), ._3(multiplexer_3_out), ._4(multiplexer_4_out),
    ._5(multiplexer_5_out), ._6(multiplexer_6_out), ._7(multiplexer_7_out), ._8(multiplexer_8_out),
    .display_in(display_1_display_in), .clear_screen(display_1_clear_screen));
  _7_Segment_Display u_7_segment_display_3 (
    .g(COMPUTER_SCORE_g), .f(COMPUTER_SCORE_f), .a(COMPUTER_SCORE_a_2), .b(COMPUTER_SCORE_b_2),
    .e(COMPUTER_SCORE_e), .d(COMPUTER_SCORE_d_2), .c(COMPUTER_SCORE_c_2));  // open: dp
  TTY tty_1 (.data(display_1_display_in[6:0]), .clk(clock_1_out), .clr(display_1_clear_screen));  // open: we
endmodule

module control_unit_get_word (
  input  replay,
  input  START,
  input  ENTER,
  output L1,
  output L2,
  output L3,
  output L4,
  output L5,
  output L6,
  output L7,
  output L8,
  output L_N,
  output \begin 
);

  wire ADDED_out, CLK_out, e_start_prime_out, N0_2_out, N0_out, N1_out, N2_out, N3_out, N4_out, not_1_out,
       not_2_out, or_2_out, or_3_out, or_4_out, s0_out, s1__prime_start_prime_out,
       s1_e_prime__start_prime_out, s1_out, s1_start_prime_out, s2_2_out, s2_out,
       s3_e_prime__start_prime_out, s3_e_start_prime_out, s3_out, s4_2_out, s4_out, s5_e__start_prime_out,
       s5_start_prime_out, s6_out, s7_e_prime__start_prime_out, s7_e_start_prime_2_out, s7_e_start_prime_out,
       s8_out, s9_e_prime__start_prime_out, s9_start_prime_out, s10_out, s11_e_prime__start_prime_out,
       s11_e_start_prime_out, s12_out, s13_e_prime__start_prime_out, s14_out, S15r_out, s16_out,
       start_prime__s3_out;
  wire [4:0] not_6_out, State_reg_q;

  Clock CLK (.out(CLK_out));
  Register #(.width(5)) State_reg (.D(not_6_out), .en(1'b1), .Q(State_reg_q), .clk(CLK_out));  // open: clr
  or or_1 (L_N, s8_out, s2_2_out, s4_2_out, s6_out, s10_out, s12_out, s14_out, s16_out);
  not s0 (s0_out, State_reg_q[0]);
  not s1 (s1_out, State_reg_q[1]);
  not s2 (s2_out, State_reg_q[2]);
  not s3 (s3_out, State_reg_q[3]);
  not s4 (s4_out, State_reg_q[4]);
  and s0_2 (L1, s0_out, s1_out, s4_out, s2_out, s3_out);
  and s1_2 (L2, State_reg_q[0], s1_out, s4_out, s2_out, s3_out);
  and s2_2 (s2_2_out, s0_out, State_reg_q[1], s4_out, s3_out, s2_out);
  and s3_2 (L3, State_reg_q[0], State_reg_q[1], s4_out, s2_out, s3_out);
  and s4_2 (s4_2_out, s3_out, State_reg_q[2], s4_out, s1_out, s0_out);
  and s5 (L4, s3_out, State_reg_q[2], s4_out, s1_out, State_reg_q[0]);
  and s6 (s6_out, s3_out, State_reg_q[2], s4_out, State_reg_q[1], s0_out);
  and s7 (L5, s3_out, State_reg_q[2], s4_out, State_reg_q[1], State_reg_q[0]);
  and s8 (s8_out, State_reg_q[3], s2_out, s4_out, s1_out, s0_out);
  and s9 (L6, State_reg_q[3], s2_out, s4_out, s1_out, State_reg_q[0]);
  and s10 (s10_out, State_reg_q[3], s2_out, s4_out, State_reg_q[1], s0_out);
  and s11 (L7, State_reg_q[3], s2_out, s4_out, State_reg_q[1], State_reg_q[0]);
  and s12 (s12_out, State_reg_q[3], State_reg_q[2], s4_out, s1_out, s0_out);
  and s13 (L8, State_reg_q[3], State_reg_q[2], s4_out, s1_out, State_reg_q[0]);
  and s14 (s14_out, State_reg_q[3], State_reg_q[2], s4_out, State_reg_q[1], s0_out);
  and s15 (\begin , State_reg_q[3], State_reg_q[2], s4_out, State_reg_q[1], State_reg_q[0]);
  and s16 (s16_out, s0_out, s1_out, s2_out, s2_out, State_reg_q[4]);
  and S15r (S15r_out, replay, \begin );
  not not_1 (not_1_out, START);
  and s1__prime_start_prime (s1__prime_start_prime_out, not_1_out, L2);
  and s3_e_prime__start_prime (s3_e_prime__start_prime_out, not_1_out, L3, not_2_out);
  and s7_e_start_prime (s7_e_start_prime_out, L5, ENTER, not_1_out);
  and s9_start_prime (s9_start_prime_out, L6, not_1_out);
  and s11_e_prime__start_prime (s11_e_prime__start_prime_out, L7, not_1_out, not_2_out);
  or N4 (N4_out, s16_out, L1);
  and e_start_prime (e_start_prime_out, not_1_out, ENTER);
  or or_2 (or_2_out, s16_out, s6_out, s2_2_out, s4_2_out, s8_out, s10_out, s12_out, s14_out);
  and N4_2 (not_6_out[4], N4_out, ENTER);
  and s1_start_prime (s1_start_prime_out, L2, not_1_out);
  and start_prime__s3 (start_prime__s3_out, L3, not_1_out);
  and s5_start_prime (s5_start_prime_out, L4, not_1_out);
  and s7_e_prime__start_prime (s7_e_prime__start_prime_out, not_2_out, not_1_out, L5);
  and s1_e_prime__start_prime (s1_e_prime__start_prime_out, not_2_out, not_1_out, L2);
  and s3_e_start_prime (s3_e_start_prime_out, not_1_out, ENTER, L3);
  and s5_e__start_prime (s5_e__start_prime_out, L4, not_2_out, not_1_out);
  and s7_e_start_prime_2 (s7_e_start_prime_2_out, L5, ENTER, not_1_out);
  and s9_e_prime__start_prime (s9_e_prime__start_prime_out, L6, not_2_out, not_1_out);
  and s11_e_start_prime (s11_e_start_prime_out, ENTER, not_1_out, L7);
  and s13_e_prime__start_prime (s13_e_prime__start_prime_out, not_2_out, not_1_out, L8);
  or or_3 (or_3_out, L2, L3, L4, L5, L6, L7, L8);
  and ADDED (ADDED_out, ENTER, or_2_out);
  not not_2 (not_2_out, ENTER);
  or or_4 (or_4_out, L1, S15r_out);
  and N0 (N0_out, e_start_prime_out, or_3_out);
  or N1 (N1_out, s16_out, s5_e__start_prime_out, L1, s1_e_prime__start_prime_out, s3_e_start_prime_out, s4_2_out, S15r_out, s7_e_start_prime_2_out, s8_out, s9_e_prime__start_prime_out, s11_e_start_prime_out, s12_out, s13_e_prime__start_prime_out);
  or N2 (N2_out, s1__prime_start_prime_out, s2_2_out, s3_e_prime__start_prime_out, L1, s7_e_start_prime_out, S15r_out, s9_start_prime_out, s10_out, s11_e_prime__start_prime_out, s8_out, s16_out);
  or N0_2 (N0_2_out, N0_out, S15r_out, ADDED_out, L1);
  not not_3 (not_6_out[3], N3_out);
  or N3 (N3_out, or_4_out, s1_start_prime_out, s2_2_out, start_prime__s3_out, s16_out, s4_2_out, s5_start_prime_out, s6_out, s7_e_prime__start_prime_out);
  not not_4 (not_6_out[1], N1_out);
  not not_5 (not_6_out[2], N2_out);
  not not_6 (not_6_out[0], N0_2_out);
endmodule

module keyboard (
  input  A,
  input  B,
  input  C,
  input  D,
  input  E,
  input  F,
  input  G,
  input  H,
  input  I,
  input  J,
  input  K,
  input  L,
  input  M,
  input  N,
  input  O,
  input  P,
  input  Q,
  input  R,
  input  S,
  input  T,
  input  U,
  input  V,
  input  W,
  input  X,
  input  Y,
  input  Z,
  output [7:0] key_output
);

  wire [4:0] priority_encoder_1_out;

  Priority_Encoder #(.select(5)) priority_encoder_1 (
    .in0(A), .in1(B), .in2(C), .in3(D), .in4(E), .in5(F), .in6(G), .in7(H), .in8(I), .in9(J), .in10(K),
    .in11(L), .in12(M), .in13(N), .in14(O), .in15(P), .in16(Q), .in17(R), .in18(S), .in19(T), .in20(U),
    .in21(V), .in22(W), .in23(X), .in24(Y), .in25(Z), .out(priority_encoder_1_out));  // open: in26, in27, in28, in29, in30, in31, gs, en_out, en_in
  Multiplexer #(.select(5), .width(8)) multiplexer_1 (
    .in0(8'h41), .in1(8'h42), .in2(8'h43), .in3(8'h44), .in4(8'h45), .in5(8'h46), .in6(8'h47), .in7(8'h48),
    .in8(8'h49), .in9(8'h4a), .in10(8'h4b), .in11(8'h4c), .in12(8'h4d), .in13(8'h4e), .in14(8'h4f),
    .in15(8'h50), .in16(8'h51), .in17(8'h52), .in18(8'h53), .in19(8'h54), .in20(8'h55), .in21(8'h56),
    .in22(8'h57), .in23(8'h58), .in24(8'h59), .in25(8'h5a), .out(key_output), .sel(priority_encoder_1_out));  // open: in26, in27, in28, in29, in30, in31, en
endmodule

module datapath_get_word (
  input  L_N,
  input  L_1,
  input  L_2,
  input  L_3,
  input  [7:0] lkey_input,
  input  L_4,
  input  L_5,
  input  L_6,
  input  L_7,
  input  L_8,
  input  CLK,
  input  ClearWord,
  output [3:0] n_letters,
  output [7:0] letter_1,
  output [7:0] letter_2,
  output [7:0] letter_3,
  output [7:0] letter_4,
  output [7:0] letter_5,
  output [7:0] letttere_6,
  output [7:0] letter_7,
  output [7:0] letter_8
);

  wire undriven;

  Counter #(.width(4), .max('hf)) counter_1 (
    .load(undriven), .D(4'b1000), .count(1'b1), .Q(n_letters), .clk(L_N), .clr(ClearWord));  // open: carry
  Register u_letter_1 (.D(lkey_input), .en(L_1), .Q(letter_1), .clk(CLK), .clr(ClearWord));
  Register u_letter_2 (.D(lkey_input), .en(L_2), .Q(letter_2), .clk(CLK), .clr(ClearWord));
  Register u_letter_3 (.D(lkey_input), .en(L_3), .Q(letter_3), .clk(CLK), .clr(ClearWord));
  Register u_letter_4 (.D(lkey_input), .en(L_4), .Q(letter_4), .clk(CLK), .clr(ClearWord));
  Register u_letter_5 (.D(lkey_input), .en(L_5), .Q(letter_5), .clk(CLK), .clr(ClearWord));
  Register letter_6 (.D(lkey_input), .en(L_6), .Q(letttere_6), .clk(CLK), .clr(ClearWord));
  Register u_letter_7 (.D(lkey_input), .en(L_7), .Q(letter_7), .clk(CLK), .clr(ClearWord));
  Register u_letter_8 (.D(lkey_input), .en(L_8), .Q(letter_8), .clk(CLK), .clr(ClearWord));
endmodule

module display_7_segment (
  input  D,
  input  C,
  input  B,
  input  A,
  output a_2,
  output b_2,
  output c_2,
  output d_2,
  output e,
  output f,
  output g
);

  wire and_1_out, and_2_out, and_3_out, and_4_out, and_5_out, and_6_out, and_7_out, and_8_out, and_9_out,
       and_10_out, and_11_out, and_12_out, and_13_out, and_14_out, and_15_out, and_16_out, not_1_out,
       not_2_out, not_3_out, not_4_out, not_5_out, not_6_out, not_7_out, not_8_out, not_9_out, not_10_out,
       not_11_out, not_12_out, not_13_out, not_14_out, not_15_out, not_16_out, not_17_out, not_18_out,
       not_19_out, not_20_out, not_21_out;

  not not_1 (not_1_out, C);
  and and_1 (and_1_out, not_1_out, not_2_out);
  not not_2 (not_2_out, A);
  and and_2 (and_2_out, C, A);
  not not_3 (not_3_out, C);
  not not_4 (not_4_out, B);
  and and_3 (and_3_out, not_4_out, not_5_out);
  not not_5 (not_5_out, A);
  and and_4 (and_4_out, B, A);
  not not_6 (not_6_out, B);
  or or_1 (c_2, not_6_out, A, C);
  not not_7 (not_7_out, C);
  and and_5 (and_5_out, not_7_out, not_8_out);
  not not_8 (not_8_out, A);
  not not_9 (not_9_out, C);
  and and_6 (and_6_out, not_9_out, B);
  and and_7 (and_7_out, B, not_10_out);
  not not_10 (not_10_out, A);
  and and_8 (and_8_out, C, not_11_out, A);
  not not_11 (not_11_out, B);
  not not_12 (not_12_out, C);
  and and_9 (and_9_out, not_12_out, not_13_out);
  not not_13 (not_13_out, A);
  and and_10 (and_10_out, B, not_14_out);
  not not_14 (not_14_out, A);
  not not_15 (not_15_out, B);
  and and_11 (and_11_out, not_15_out, not_16_out);
  not not_16 (not_16_out, A);
  and and_12 (and_12_out, C, not_17_out);
  not not_17 (not_17_out, B);
  and and_13 (and_13_out, C, not_18_out);
  not not_18 (not_18_out, A);
  not not_19 (not_19_out, C);
  and and_14 (and_14_out, not_19_out, B);
  and and_15 (and_15_out, C, not_20_out);
  not not_20 (not_20_out, B);
  and and_16 (and_16_out, C, not_21_out);
  not not_21 (not_21_out, A);
  or or_2 (a_2, and_1_out, B, and_2_out, D);
  or or_3 (b_2, not_3_out, and_3_out, and_4_out);
  or or_4 (d_2, and_5_out, and_6_out, and_7_out, and_8_out, D);
  or or_5 (e, and_9_out, and_10_out);
  or or_6 (f, and_11_out, and_12_out, and_13_out, D);
  or or_7 (g, and_14_out, and_15_out, and_16_out, D);
endmodule

// check foo DP
module datapath_check_word (
  input  [3:0] letter_n,
  input  count_n,
  input  clear_count,
  input  [7:0] T1,
  input  [7:0] L1,
  input  [7:0] T2,
  input  [7:0] L2,
  input  [7:0] T3,
  input  s_w_t,
  input  [7:0] L3,
  input  [7:0] T4,
  input  [7:0] guess,
  input  [7:0] L4,
  input  [7:0] T5,
  input  [7:0] L5,
  input  [7:0] t6,
  input  [7:0] L6,
  input  [7:0] T7,
  input  [7:0] L7,
  input  [7:0] T8,
  input  [7:0] L8,
  output [3:0] counter,
  output eq_count,
  output EQ_L_T_G,
  output [7:0] current_letter
);

  wire [7:0] multiplexer_1_out, multiplexer_3_out;

  Counter #(.width(4), .max('hf)) count (
    .count(1'b1), .Q(counter), .clk(count_n), .clr(clear_count));  // open: load, D, carry
  Comparator #(.width(4), .mode("unsigned")) comparator_1 (.a(counter), .b(letter_n), .eq(eq_count));  // open: gt, lt
  Multiplexer #(.select(3), .width(8)) multiplexer_1 (
    .in0(T1), .in1(T2), .in2(T3), .in3(T4), .in4(T5), .in5(t6), .in6(T7), .in7(T8), .out(multiplexer_1_out),
    .sel(counter[2:0]));  // open: en
  Multiplexer #(.select(3), .width(8)) multiplexer_2 (
    .in0(L1), .in1(L2), .in2(L3), .in3(L4), .in4(L5), .in5(L6), .in6(L7), .in7(L8), .out(current_letter),
    .sel(counter[2:0]));  // open: en
  Multiplexer #(.width(8)) multiplexer_3 (
    .in0(multiplexer_1_out), .in1(current_letter), .out(multiplexer_3_out), .sel(s_w_t));  // open: en
  Comparator #(.mode("unsigned")) comparator_2 (.a(multiplexer_3_out), .b(guess), .eq(EQ_L_T_G));  // open: gt, lt
endmodule

// check CU
module control_unit_check_word (
  input  eq_l_t_g,
  input  eq_count,
  input  begin_check,
  output count_n,
  output mistake,
  output swt,
  output L_T_new,
  output correct,
  output clear_count,
  output checked
);

  wire and_1_out, and_2_out, and_3_out, and_4_out, and_5_out, and_6_out, and_7_out, and_8_out, clock_1_out,
       N2_out, not_1_out, not_2_out, not_3_out, not_4_out, not_5_out, not_6_out, S7_out;
  wire [2:0] N0_out, State_reg_q;

  Clock clock_1 (.out(clock_1_out));
  not not_1 (not_1_out, eq_l_t_g);
  Register #(.width(3)) State_reg (.D(N0_out), .en(1'b1), .Q(State_reg_q), .clk(clock_1_out));  // open: clr
  not not_2 (not_2_out, eq_count);
  not not_3 (not_3_out, begin_check);
  not not_4 (not_4_out, State_reg_q[0]);
  not not_5 (not_5_out, State_reg_q[1]);
  not not_6 (not_6_out, State_reg_q[2]);
  and S7 (S7_out, State_reg_q[2], State_reg_q[1], State_reg_q[0]);
  and S0 (clear_count, not_4_out, not_5_out, not_6_out);
  and S1 (swt, not_6_out, not_5_out, State_reg_q[0]);
  and S2 (mistake, not_6_out, State_reg_q[1], not_4_out);
  and S3 (L_T_new, not_6_out, State_reg_q[1], State_reg_q[0]);
  and S4 (correct, State_reg_q[2], not_5_out, not_4_out);
  and S5 (count_n, State_reg_q[2], not_5_out, State_reg_q[0]);
  and S6 (checked, State_reg_q[2], State_reg_q[1], not_4_out);
  and and_1 (and_1_out, S7_out, eq_count);
  and and_2 (and_2_out, S7_out, not_2_out);
  // OR_Gate MISTAKE_CAN_BE is placed but not wired
  and and_3 (and_3_out, S7_out, not_2_out);
  and and_4 (and_4_out, clear_count, not_3_out);
  and and_5 (and_5_out, clear_count, begin_check);
  and and_6 (and_6_out, L_T_new, eq_l_t_g);
  and and_7 (and_7_out, clear_count, begin_check);
  and and_8 (and_8_out, swt, eq_l_t_g);
  or N2 (N2_out, swt, and_3_out, checked, and_4_out);
  or N1 (N0_out[1], swt, count_n, and_1_out, and_5_out, and_6_out);
  or N0 (N0_out[0], and_2_out, mistake, correct, and_7_out, and_8_out, count_n);
  not not_7 (N0_out[2], N2_out);
endmodule

module test_small (
  input  [7:0] T1,
  input  [7:0] T2,
  input  [7:0] T3,
  input  [7:0] T4,
  input  [7:0] T5,
  input  [7:0] t6,
  input  [7:0] T7,
  input  [7:0] T8
);

  wire datapath_check_word_1_p1, datapath_check_word_1_p2;

  control_unit_check_word control_unit_check_word_1 (
    .eq_l_t_g(datapath_check_word_1_p2), .eq_count(datapath_check_word_1_p1));  // open: begin_check, count_n, mistake, swt, L_T_new, correct, clear_count, checked
  // datapath_check_word datapath_check_word_1: pin names not known; wires that end beside it: datapath_check_word_1_p1, datapath_check_word_1_p2
endmodule

// main_DP
module main_loop_datapath (
  input  mistake_incrt,
  input  cllear_mistake,
  input  [3:0] n_letter,
  input  enable_mistake,
  input  enable_correct,
  input  [3:0] S_COUNT,
  input  S_L_1,
  input  S_L_0,
  input  S_L,
  input  clear_reset,
  input  [7:0] new_t_from_check,
  input  L_T_update,
  input  [7:0] guess_key_in,
  input  L_GUESS,
  input  CLK,
  output lost,
  output [3:0] mistake_out,
  output [3:0] correct_out,
  output won,
  output [7:0] T_1,
  output [3:0] mistake_count,
  output [7:0] T_2,
  output [7:0] T_3,
  output [7:0] T_4,
  output [7:0] T_5,
  output [7:0] T_6,
  output [7:0] T_7,
  output [7:0] T_8,
  output [7:0] guess_out
);

  wire comparator_1_eq, decoder_custom_1_t1, decoder_custom_1_t2, decoder_custom_1_t3, decoder_custom_1_t4,
       decoder_custom_1_t5, decoder_custom_1_t6, decoder_custom_1_t7, decoder_custom_1_t8;
  wire [3:0] adder_1_out, multiplexer_1_out, subtractor_1_out;
  wire [7:0] multiplexer_2_out, T_TO_UPDATE_q;

  decoder_custom decoder_custom_1 (
    .c0(multiplexer_1_out[0]), .c1(multiplexer_1_out[1]), .c2(multiplexer_1_out[2]),
    .c3(multiplexer_1_out[3]), .t1(decoder_custom_1_t1), .t2(decoder_custom_1_t2), .t3(decoder_custom_1_t3),
    .t4(decoder_custom_1_t4), .t5(decoder_custom_1_t5), .t6(decoder_custom_1_t6), .t7(decoder_custom_1_t7),
    .t8(decoder_custom_1_t8));
  Multiplexer #(.select(2), .width(4)) multiplexer_1 (
    .in0(4'b1001), .in1(4'b1000), .in2(S_COUNT), .out(multiplexer_1_out), .sel({S_L_1, S_L_0}));  // open: in3, en
  Register T_TO_UPDATE (.D(new_t_from_check), .en(CLK), .Q(T_TO_UPDATE_q), .clk(L_T_update));  // open: clr
  Multiplexer #(.width(8)) multiplexer_2 (
    .in0(T_TO_UPDATE_q), .in1(8'h7e), .out(multiplexer_2_out), .sel(S_L));  // open: en
  Counter #(.width(4), .max('hf)) counter_1 (
    .count(enable_mistake), .Q(mistake_count), .clk(mistake_incrt), .clr(cllear_mistake));  // open: load, D, carry
  Comparator #(.width(4)) comparator_1 (.a(subtractor_1_out), .b(n_letter), .eq(comparator_1_eq));  // open: gt, lt
  Counter #(.width(4), .max('hf)) counter_2 (
    .count(enable_mistake), .Q(mistake_out), .clk(comparator_1_eq), .clr(clear_reset));  // open: load, D, carry
  Register #(.width(4)) State_reg (.D(adder_1_out), .en(enable_correct), .Q(correct_out), .clk(CLK), .clr(clear_reset));
  Register u_T_1 (.D(multiplexer_2_out), .en(decoder_custom_1_t1), .Q(T_1), .clk(CLK));  // open: clr
  Register T2 (.D(multiplexer_2_out), .en(decoder_custom_1_t2), .Q(T_2), .clk(CLK));  // open: clr
  Register u_T_3 (.D(multiplexer_2_out), .en(decoder_custom_1_t3), .Q(T_3), .clk(CLK));  // open: clr
  Register u_T_4 (.D(multiplexer_2_out), .en(decoder_custom_1_t4), .Q(T_4), .clk(CLK));  // open: clr
  Register u_T_5 (.D(multiplexer_2_out), .en(decoder_custom_1_t5), .Q(T_5), .clk(CLK));  // open: clr
  Register u_T_6 (.D(multiplexer_2_out), .en(decoder_custom_1_t6), .Q(T_6), .clk(CLK));  // open: clr
  Register u_T_7 (.D(multiplexer_2_out), .en(decoder_custom_1_t7), .Q(T_7), .clk(CLK));  // open: clr
  Register u_T_8 (.D(multiplexer_2_out), .en(decoder_custom_1_t8), .Q(T_8), .clk(CLK));  // open: clr
  Register letter_4 (.D(guess_key_in), .en(L_GUESS), .Q(guess_out), .clk(CLK));  // open: clr
  Comparator #(.width(4)) comparator_2 (.a(mistake_out), .b(4'b1010), .eq(lost));  // open: gt, lt
  Comparator #(.width(4)) comparator_3 (.a(correct_out), .b(n_letter), .eq(won));  // open: gt, lt
  Subtractor #(.width(4)) subtractor_1 (.a(mistake_count), .b(4'b0001), .out(subtractor_1_out));  // open: bin, bout
  Adder #(.width(4)) adder_1 (.a(correct_out), .b(4'b0001), .out(adder_1_out));  // open: cin, cout
endmodule

module decoder_custom (
  input  c0,
  input  c1,
  input  c2,
  input  c3,
  output t1,
  output t2,
  output t3,
  output t4,
  output t5,
  output t6,
  output t7,
  output t8
);

  wire and_1_out, and_2_out, and_3_out, and_4_out, and_5_out, and_6_out, and_7_out, and_8_out, and_9_out,
       and_10_out, and_11_out, and_12_out, and_13_out, and_14_out, and_15_out, and_16_out, and_17_out,
       and_18_out, and_20_out, and_21_out, and_22_out, and_23_out, and_24_out, and_25_out, and_26_out,
       and_27_out, not_1_out, not_2_out, not_3_out, not_4_out, not_5_out, not_6_out, not_7_out, not_8_out,
       not_9_out, not_10_out, not_11_out, not_12_out, not_13_out, not_14_out, not_15_out, not_16_out,
       not_17_out, not_18_out, not_19_out, not_20_out;

  not not_1 (not_1_out, c0);
  not not_2 (not_2_out, c1);
  not not_3 (not_3_out, c2);
  not not_4 (not_4_out, c3);
  not not_5 (not_5_out, c0);
  and and_1 (and_1_out, not_5_out, c3);
  and and_2 (and_2_out, c2, c3);
  not not_6 (not_6_out, c0);
  and and_3 (and_3_out, not_6_out, c1, not_7_out);
  not not_7 (not_7_out, c2);
  and and_4 (and_4_out, c1, c3);
  not not_8 (not_8_out, c0);
  and and_5 (and_5_out, not_8_out, c3);
  and and_6 (and_6_out, c2, c3);
  and and_7 (and_7_out, c0, c1, not_9_out);
  not not_9 (not_9_out, c2);
  not not_10 (not_10_out, c0);
  and and_8 (and_8_out, not_10_out, c3);
  not not_11 (not_11_out, c0);
  and and_9 (and_9_out, not_11_out, not_12_out, c2);
  not not_12 (not_12_out, c1);
  and and_10 (and_10_out, c2, c3);
  and and_11 (and_11_out, c1, c3);
  not not_13 (not_13_out, c0);
  and and_12 (and_12_out, not_13_out, c3);
  and and_13 (and_13_out, c1, c3);
  and and_14 (and_14_out, c0, not_14_out, c2);
  not not_14 (not_14_out, c1);
  not not_15 (not_15_out, c0);
  and and_15 (and_15_out, not_15_out, c3);
  and and_16 (and_16_out, c2, c3);
  and and_17 (and_17_out, c1, c3);
  not not_16 (not_16_out, c0);
  and and_18 (and_18_out, not_16_out, c1, c2);
  not not_17 (not_17_out, c2);
  not not_18 (not_18_out, c1);
  and and_19 (t1, not_17_out, not_18_out, not_19_out);
  not not_19 (not_19_out, c0);
  not not_20 (not_20_out, c0);
  and and_20 (and_20_out, not_20_out, c3);
  and and_21 (and_21_out, c2, c3);
  and and_22 (and_22_out, c1, c3);
  and and_23 (and_23_out, c0, c1, c2);
  and and_24 (and_24_out, not_1_out, c3);
  and and_25 (and_25_out, c2, c3);
  and and_26 (and_26_out, c1, c3);
  and and_27 (and_27_out, c0, not_2_out, not_3_out, not_4_out);
  or or_1 (t3, and_1_out, and_2_out, and_3_out, and_4_out);
  or or_2 (t4, and_5_out, and_6_out, and_7_out);
  or or_3 (t5, and_8_out, and_9_out, and_10_out, and_11_out);
  or or_4 (t6, and_12_out, and_13_out, and_14_out);
  or or_5 (t7, and_15_out, and_16_out, and_17_out, and_18_out);
  or or_6 (t8, and_20_out, and_21_out, and_22_out, and_23_out);
  or or_7 (t2, and_24_out, and_25_out, and_26_out, and_27_out);
endmodule

// main_CU
module main_loop_control_unit (
  input  \begin ,
  input  e,
  input  res,
  input  checked,
  input  won,
  input  lsot,
  output clear_reset,
  output S_L_0,
  output S_L,
  output clear_mistake,
  output L_guess,
  output start_check_fun
);

  wire and_2_out, and_3_out, and_4_out, and_5_out, and_6_out, and_7_out, and_8_out, and_9_out, and_10_out,
       and_11_out, and_12_out, and_13_out, and_14_out, and_15_out, clock_1_out, not_1_out, not_2_out,
       not_3_out, not_4_out, not_5_out, not_6_out, not_7_out, not_8_out, not_9_out, S5_out, S6_out, S7_out,
       undriven, undriven_2, undriven_3, xor_1_out;
  wire [2:0] N0_out, State_reg_q;

  Clock clock_1 (.out(clock_1_out));
  Register #(.width(3)) State_reg (.D(N0_out), .en(1'b1), .Q(State_reg_q), .clk(clock_1_out));  // open: clr
  not not_1 (not_1_out, State_reg_q[0]);
  not not_2 (not_2_out, State_reg_q[1]);
  not not_3 (not_3_out, State_reg_q[2]);
  and S0 (clear_reset, not_1_out, not_2_out, not_3_out);
  and S1 (S_L, not_3_out, not_2_out, State_reg_q[0]);
  and S2 (L_guess, not_3_out, State_reg_q[1], not_1_out);
  and S3 (start_check_fun, not_3_out, State_reg_q[1], State_reg_q[0]);
  and S4 (clear_mistake, State_reg_q[2], not_2_out, not_1_out);
  and S5 (S5_out, State_reg_q[2], not_2_out, State_reg_q[0]);
  and S6 (S6_out, State_reg_q[2], State_reg_q[1], not_1_out);
  and S7 (S7_out, State_reg_q[0], State_reg_q[1], State_reg_q[2]);
  // AND_Gate and_1 has open pins: in0=undriven, in1=undriven_3, in2=undriven_2, out=open
  and and_2 (and_2_out, clear_reset, not_5_out, \begin );
  and and_3 (and_3_out, L_guess, e);
  and and_4 (and_4_out, start_check_fun, not_7_out);
  and and_5 (and_5_out, clear_mistake, not_9_out, won);
  and and_6 (and_6_out, S5_out, not_6_out);
  not not_4 (not_4_out, \begin );
  not not_5 (not_5_out, e);
  not not_6 (not_6_out, res);
  not not_7 (not_7_out, checked);
  not not_8 (not_8_out, won);
  not not_9 (not_9_out, lsot);
  and and_7 (and_7_out, e, clear_mistake);
  and and_8 (and_8_out, checked, start_check_fun);
  xor xor_1 (xor_1_out, lsot, won);
  and and_9 (and_9_out, not_6_out, S5_out);
  and and_10 (and_10_out, not_6_out, S6_out);
  and and_11 (and_11_out, clear_mistake, not_5_out);
  and and_12 (and_12_out, start_check_fun, not_7_out);
  and and_13 (and_13_out, clear_mistake, won, not_9_out);
  and and_14 (and_14_out, S6_out, not_6_out);
  or N2 (N0_out[2], and_10_out, and_9_out, and_7_out, and_8_out, and_15_out);
  and and_15 (and_15_out, xor_1_out, clear_mistake);
  or N1 (N0_out[1], and_12_out, S_L, L_guess, and_13_out, and_14_out, and_11_out);
  or N0 (N0_out[0], and_2_out, and_3_out, and_4_out, and_5_out, and_6_out);

  assign S_L_0 = S_L;
endmodule

module display (
  input  [7:0] _1,
  input  [7:0] _2,
  input  [7:0] _3,
  input  [7:0] _4,
  input  [7:0] _5,
  input  [7:0] _6,
  input  [7:0] _7,
  input  [7:0] _8,
  output [7:0] display_in,
  output clear_screen
);

  wire clock_1_out, comparator_1_eq, not_1_out;
  wire [2:0] counter_1_q;
  wire [7:0] multiplexer_1_out;

  Counter #(.width(3), .max('h7)) counter_1 (
    .Q(counter_1_q), .carry(clear_screen), .clk(clock_1_out));  // open: load, D, count, clr
  Clock clock_1 (.out(clock_1_out));
  Multiplexer #(.select(3), .width(8)) multiplexer_1 (
    .in0(_1), .in1(_2), .in2(_3), .in3(_4), .in4(_5), .in5(_6), .in6(_7), .in7(_8), .out(multiplexer_1_out),
    .sel(counter_1_q));  // open: en
  Comparator comparator_1 (.a(multiplexer_1_out), .b({8{1'b0}}), .eq(comparator_1_eq));  // open: gt, lt
  not not_1 (not_1_out, comparator_1_eq);
  Multiplexer #(.width(8)) multiplexer_2 (
    .in0(8'h7e), .in1(multiplexer_1_out), .out(display_in), .sel(not_1_out));  // open: en
endmodule

module led_matrix (
  input  [3:0] select_mistake,
  output [7:0] col_1,
  output [7:0] col_2,
  output [7:0] col_3,
  output [7:0] col_4,
  output [7:0] col_5
);

  Multiplexer #(.select(4), .width(8)) multiplexer_1 (
    .in0({8{1'b0}}), .in1({8{1'b1}}), .in2({8{1'b1}}), .in3({8{1'b1}}), .in4({8{1'b1}}), .in5({8{1'b1}}),
    .in6({8{1'b1}}), .in7({8{1'b1}}), .in8({8{1'b1}}), .in9({8{1'b1}}), .out(col_1), .sel(select_mistake));  // open: in10, in11, in12, in13, in14, in15, en
  Multiplexer #(.select(4), .width(8)) multiplexer_2 (
    .in0({8{1'b0}}), .in1({8{1'b0}}), .in2(8'h80), .in3(8'h80), .in4(8'h80), .in5(8'h80), .in6(8'h80),
    .in7(8'h80), .in8(8'h80), .in9(8'h80), .out(col_2), .sel(select_mistake));  // open: in10, in11, in12, in13, in14, in15, en
  Multiplexer #(.select(4), .width(8)) multiplexer_3 (
    .in0({8{1'b0}}), .in1({8{1'b0}}), .in2(8'h80), .in3(8'h80), .in4(8'h80), .in5(8'h88), .in6(8'h88),
    .in7(8'h88), .in8(8'h89), .in9(8'h89), .out(col_3), .sel(select_mistake));  // open: in10, in11, in12, in13, in14, in15, en
  Multiplexer #(.select(4), .width(8)) multiplexer_4 (
    .in0({8{1'b0}}), .in1({8{1'b0}}), .in2(8'h80), .in3(8'he0), .in4(8'hf0), .in5(8'hf0), .in6(8'hf0),
    .in7(8'hf6), .in8(8'hf6), .in9(8'hf6), .out(col_4), .sel(select_mistake));  // open: in10, in11, in12, in13, in14, in15, en
  Multiplexer #(.select(4), .width(8)) multiplexer_5 (
    .in0({8{1'b0}}), .in1({8{1'b0}}), .in2(8'h80), .in3(8'h80), .in4(8'h80), .in5(8'h80), .in6(8'h88),
    .in7(8'h88), .in8(8'h88), .in9(8'h89), .out(col_5), .sel(select_mistake));  // open: in10, in11, in12, in13, in14, in15, en
endmodule
